# Fritzing sketch eksamenEmbedded (saved by Fritzing 0.9.4)
breadboards: 1

parts:
  Part1 = Photon
  J1 = Piezo Speaker
  R1 = Resistor [tolerance=±5% resistance=220 package="2010 [SMD]"]
  LED1 = RGB LED (com. cathode, rbg) [package="5 mm [THT]"]
  R2 = Resistor [tolerance=±5% resistance=220 package="2010 [SMD]"]
  R3 = Resistor [tolerance=±5% resistance=220 package="2010 [SMD]"]
  R4 = Resistor [tolerance=±5% resistance=220 package="2010 [SMD]"]
  PIR1 = PIR sensor
  S1 = Pushbutton [package="[SMD]"]
  DS1 = DS18B20 1-Wire Temperature Sensor [part_number=DS18B20]
  R5 = Resistor [tolerance=±5% resistance=220 package="0603 [SMD]"]

nets:
  GND: Part1.GND, J1.pin1, LED1.common_cathode, PIR1.GND, S1.Pin_1, S1.Pin_2, DS1.GND
  VDD: Part1.VIN, PIR1.VDD, DS1.VDD, R5.Pin_0
  N1: Part1.D0, PIR1.SIG
  N2: Part1.D1, R1.Pin_1
  N3: Part1.D2, R2.Pin_1
  N4: Part1.D3, R4.Pin_1
  N5: Part1.D4, R3.Pin_1
  N6: Part1.D5, S1.Pin_3, S1.Pin_4
  N7: Part1.D6, DS1.DQ, R5.Pin_1
  N8: J1.pin2, R1.Pin_0
  N9: LED1.red_anode, R2.Pin_0
  N10: LED1.blue_anode, R4.Pin_0
  N11: LED1.green_anode, R3.Pin_0
